# Fritzing sketch sinled (saved by Fritzing 0.9.1b)

parts:
  Part1 = Arduino Uno (Rev3)
  LED1 = LED - 5mm [color="Blue (430nm)" current=25m package="5 mm [THT]"]
  R1 = Resistor [tolerance=±5% resistance=120 package=THT]

nets:
  N1: Part1.D3_PWM, R1.Pin_1
  N2: Part1.GND, LED1.cathode
